# Fritzing sketch XPrism (saved by Fritzing 0.9.3b)
breadboards: 1

parts:
  A1 = ESP32-pico-kit-v4 [part_number=ESP32--pico-kit-v4]
  S1 = Pushbutton [package="[SMD]"]
  S2 = Pushbutton [package="[SMD]"]
  S3 = Pushbutton [package="[SMD]"]
  S4 = Pushbutton [package="[SMD]"]
  A2 = lcd color display 1.3in 240x240 7pin interface [package=THT]
  元件1 = MicroSD Card Module
  ESP32_-_Front1 = ESP32 - CAM

nets:
  N1: A1.Pin_6, S1.Pin_3, S1.Pin_4
  N2: A1.Pin_7, 元件1.MISO
  N3: A1.Pin_8, S2.Pin_3, S2.Pin_4
  N4: A1.Pin_9, S3.Pin_3, S3.Pin_4
  N5: A1.Pin_10, S4.Pin_3, S4.Pin_4
  N6: A1.Pin_11, 元件1.SCK
  N7: A1.Pin_13, 元件1.MOSI
  N8: A1.Pin_15, A2.DC
  N9: A1.Pin_16, A2.RES
  GND: A1.Pin_19, A1.Pin_22, S1.Pin_1, S1.Pin_2, S2.Pin_1, S2.Pin_2, S3.Pin_1, S3.Pin_2, S4.Pin_1, S4.Pin_2, A2.GND, 元件1.GND, ESP32_-_Front1.GND
  N10: A1.Pin_20, ESP32_-_Front1.5V
  VCC: A1.Pin_21, A2.VCC, 元件1.VCC
  N11: A1.Pin_32, 元件1.CS
  N12: A1.Pin_33, A2.SCL
  N13: A1.Pin_34, A2.SDA

custom parts:
  ESP32-pico-kit-v4: ESP32-PICO-KIT is a mini development board produced by Espressif. At the core of this board is the ESP32-PICO-D4, a System-in-Package (SiP) module with complete Wi-Fi and Bluetooth functionalities.
  lcd color display 1.3in 240x240 7pin interface: 1.3 Inch Color 240 x 240 IPS TFT LCD Display Screen Module Board 7 Pin 4 Wire ST7789VW Drive IC SPI interface.
  ESP32 - CAM: The ESP32-CAM has a very competitive small-size camera module that can operate independently as a minimum system with a footprint of only 27*40.5*4.5mm and a deep sleep current of up to 6mA.
